# Fritzing sketch anti sleep alcohol vehicle accident gps gsm  (saved by Fritzing 0.9.3b)
circuit board: 37.637cm x 17.5003cm
breadboards: 1

parts:
  Part1 = Arduino Uno (Rev3) - ICSP
  J1 = Piezo Speaker
  U1 = LCD-16X2 [package=lcd-16x2_noholes]
  GSM_SIM_GPSR_SMS_SIM900_SIM1 = SIM800L [package=THT]
  R1 = Resistor [tolerance=±5% power=0.25 resistance=220 package=THT]
  U3 = GAS_SENSOR [package=mq-3]
  S1 = Momentary Switch [package=ksa_sealed_tac_switch]
  KY-1 = Keyes Relay [package=THT]
  M1 = Getriebemotor
  VCC1 = Battery block 9V
  M2 = fc-51 [package=THT]

nets:
  N1: Part1.A1, M2.pin1
  N2: Part1.D8, U1.RS
  N3: Part1.D9_PWM, U1.E
  N4: Part1.D10_PWM/SS, U1.DB4
  N5: Part1.D11_PWM/MOSI, U1.DB5
  N6: Part1.D12/MISO, U1.DB6
  N7: Part1.D13/SCK, U1.DB7
  N8: Part1.D2, GSM_SIM_GPSR_SMS_SIM900_SIM1.SIM_RXD
  N9: Part1.D3_PWM, KY-1.signal
  N10: Part1.D4, S1.2
  N11: Part1.D7, J1.pin2
  5V: Part1.5V, GSM_SIM_GPSR_SMS_SIM900_SIM1.5V, U3.A1, M2.pin3
  GND: Part1.GND, J1.pin1, U1.VSS, U1.R_W, U1.K, GSM_SIM_GPSR_SMS_SIM900_SIM1.GND, U3.B1, S1.4, M2.pin2
  N12: U1.VO, R1.Pin_0
  N13: KY-1.C, VCC1.-
  N14: KY-1.NO, M1.pin_2
  N15: M1.pin_1, VCC1.+

custom parts:
  Keyes Relay: The Keyes 5V relay module is suitable for SCM development, home appliance control. It uses a 5V~12V TIL control signal which can control DC / AC signal.
